// Logisim project semprojcpu.circ as structural Verilog: 20 circuits, main circuit ALU8
module ALU8 (
  input  [3:0] aluop,
  input  [7:0] a,
  input  [7:0] b,
  output zero,
  output [7:0] result,
  output overflow
);

  wire alu1_1_c_out, alu1_2_c_out, alu1_3_c_out, alu1_4_c_out, alu1_5_c_out, alu1_6_c_out, alu1_7_c_out,
       alumsb_1_set, or_1_out;

  alu1 alu1_1 (
    .A(aluop[3]), .B(b[0]), .out(result[0]), .b_invert(aluop[2]), .C_in(aluop[2]), .op(aluop[1:0]),
    .C_out(alu1_1_c_out), .a_invert(a[0]), .less(alumsb_1_set));
  alu1 alu1_2 (
    .A(aluop[3]), .B(b[1]), .out(result[1]), .b_invert(aluop[2]), .C_in(alu1_1_c_out), .op(aluop[1:0]),
    .C_out(alu1_2_c_out), .a_invert(a[1]), .less(1'b0));
  alu1 alu1_3 (
    .A(aluop[3]), .B(b[2]), .out(result[2]), .b_invert(aluop[2]), .C_in(alu1_2_c_out), .op(aluop[1:0]),
    .C_out(alu1_3_c_out), .a_invert(a[2]), .less(1'b0));
  alu1 alu1_4 (
    .A(aluop[3]), .B(b[3]), .out(result[3]), .b_invert(aluop[2]), .C_in(alu1_3_c_out), .op(aluop[1:0]),
    .C_out(alu1_4_c_out), .a_invert(a[3]), .less(1'b0));
  alu1 alu1_5 (
    .A(aluop[3]), .B(b[4]), .out(result[4]), .b_invert(aluop[2]), .C_in(alu1_4_c_out), .op(aluop[1:0]),
    .C_out(alu1_5_c_out), .a_invert(a[4]), .less(1'b0));
  alu1 alu1_6 (
    .A(aluop[3]), .B(b[5]), .out(result[5]), .b_invert(aluop[2]), .C_in(alu1_5_c_out), .op(aluop[1:0]),
    .C_out(alu1_6_c_out), .a_invert(a[5]), .less(1'b0));
  alu1 alu1_7 (
    .A(aluop[3]), .B(b[6]), .out(result[6]), .b_invert(aluop[2]), .C_in(alu1_6_c_out), .op(aluop[1:0]),
    .C_out(alu1_7_c_out), .a_invert(a[6]), .less(1'b0));
  aluMSB alumsb_1 (
    .A(a[7]), .B(b[7]), .less(1'b0), .out(result[7]), .set(alumsb_1_set), .oflow(overflow),
    .a_invert(aluop[3]), .b_invert(aluop[2]), .C_in(alu1_7_c_out), .op(aluop[1:0]));
  or or_1 (or_1_out, result[0], result[1], result[2], result[3], result[4], result[5], result[6], result[7]);
  not not_1 (zero, or_1_out);
endmodule

module main (
  input  On
);

  wire alu16_1_zero, CLK, clock_1_out, ex_mem_1_memread_2, ex_mem_1_memwrite_2, ex_mem_1_out_23,
       ex_mem_1_regwrite_2, ex_mem_1_zero_2, Flush, Flush_1, Flush_2, hazard_detection_1_muxsel,
       hazard_detection_1_pcifidwrite, id_ex_1_alusrc_2, id_ex_1_flush_2, id_ex_1_memread_2,
       id_ex_1_memwrite_2, id_ex_1_out_26, id_ex_1_regwrite_2, mem_wb_1_regwrite_2, not_1_out, not_2_out,
       or_2_out, or_3_out, or_4_out, RegEq, RST;
  wire [1:0] control_1_aluop, control_1_jump, control_1_memtoreg, control_1_regdst, ex_mem_1_memtoreg_2,
       ex_mem_1_out_24, forwardingunit_1_forwarda, forwardingunit_1_forwardb, id_ex_1_aluop_2,
       id_ex_1_memtoreg_2, id_ex_1_out_27, id_ex_1_regdst_2, mem_wb_1_memtoreg_2;
  wire [3:0] alucontrol_1_out_3, ex_mem_1_rd_2, id_ex_1_func_2, id_ex_1_rd_2, id_ex_1_rs_2, id_ex_1_rt_2,
       mem_wb_1_rd_2, multiplexer_8_out;
  wire [13:0] control_1_if_flush, multiplexer_4_out;
  wire [15:0] adder_1_out, adder_2_out, alu16_1_result, bit_extender_1_out, ex_mem_1_address_2,
       ex_mem_1_branchadress, ex_mem_1_pc_1_2, ex_mem_1_r1_2, ex_mem_1_rd2_2, ex_mem_1_result_2,
       id_ex_1_address_2, id_ex_1_immediate_2, id_ex_1_pc_1_2, id_ex_1_rd1_2, id_ex_1_rd2_2, if_id_1_out_7,
       mem_wb_1_data_2, mem_wb_1_pc_1_2, mem_wb_1_result_2, multiplexer_1_out, multiplexer_3_out,
       multiplexer_5_out, multiplexer_6_out, multiplexer_7_out, multiplexer_9_out, PC_q, ram_1_data,
       regfile_1_regdata1, regfile_1_regdata2;
  wire [18:0] if_id_1_out_6, rom_1_data;

  Button RESET (.out(RST));
  Clock clock_1 (.out(clock_1_out));
  Multiplexer #(.select(2), .width(16), .enable("false")) multiplexer_1 (
    .in0(multiplexer_3_out), .in1(ex_mem_1_address_2), .in2(ex_mem_1_r1_2), .out(multiplexer_1_out),
    .sel(ex_mem_1_out_24));  // open: in3
  Register #(.width(16)) PC (
    .D(multiplexer_1_out), .en(hazard_detection_1_pcifidwrite), .Q(PC_q), .clk(CLK), .clr(RST));
  Multiplexer #(.enable("false")) multiplexer_2 (.in0(1'b0), .in1(clock_1_out), .out(CLK), .sel(On));
  or or_1 (Flush, Flush_2, Flush_1);
  and and_1 (Flush_1, ex_mem_1_zero_2, ex_mem_1_out_23);
  Multiplexer #(.width(16), .enable("false")) multiplexer_3 (
    .in0(adder_1_out), .in1(ex_mem_1_branchadress), .out(multiplexer_3_out), .sel(Flush_1));
  Adder #(.width(16)) adder_1 (.a(16'h1), .b(PC_q), .out(adder_1_out));  // open: cin, cout
  ROM #(.addrWidth(16), .dataWidth(19)) rom_1 (.addr(PC_q), .data(rom_1_data));  // open: sel
  IF_ID if_id_1 (
    .in_2(rom_1_data), .in_3(adder_1_out), .out_6(if_id_1_out_6), .out_7(if_id_1_out_7), .CLK(CLK),
    .RST(or_2_out), .Write(hazard_detection_1_pcifidwrite));
  or or_2 (or_2_out, Flush, RST);
  Hazard_Detection hazard_detection_1 (
    .PCIFIDWrite(hazard_detection_1_pcifidwrite), .ID_EX_MemRead(id_ex_1_memread_2),
    .IF_ID_RegisterRs(if_id_1_out_6[15:12]), .IF_ID_RegisterRt(if_id_1_out_6[11:8]),
    .MuxSel(hazard_detection_1_muxsel), .ID_EX_RegisterRt(id_ex_1_rt_2));
  control control_1 (
    .RegDst(control_1_regdst), .Branch(control_1_if_flush[3]), .Jump(control_1_jump),
    .ALUOp(control_1_aluop), .MemtoReg(control_1_memtoreg), .OP(if_id_1_out_6[18:16]),
    .MemRead(control_1_if_flush[10]), .MemWrite(control_1_if_flush[11]), .ALUSrc(control_1_if_flush[12]),
    .RegWrite(control_1_if_flush[13]), .IF_Flush(control_1_if_flush[0]));
  Multiplexer #(.width(14), .enable("false")) multiplexer_4 (
    .in0({control_1_if_flush[13:10], control_1_memtoreg, control_1_aluop, control_1_jump, control_1_if_flush[3], control_1_regdst, control_1_if_flush[0]}),
    .in1({14{1'b0}}), .out(multiplexer_4_out), .sel(hazard_detection_1_muxsel));
  not not_1 (not_1_out, CLK);
  assign bit_extender_1_out = {{8{if_id_1_out_6[7]}}, if_id_1_out_6[7:0]};  // Bit_Extender bit_extender_1
  _16eq u_16eq_1 (.in_1(regfile_1_regdata1), .in_2(regfile_1_regdata2), .out_3(RegEq));
  RegFile regfile_1 (
    .RegRead1(if_id_1_out_6[15:12]), .RegRead2(if_id_1_out_6[11:8]), .RegWrite_2(mem_wb_1_rd_2),
    .DIn(multiplexer_9_out), .RegData1(regfile_1_regdata1), .RegData2(regfile_1_regdata2),
    .RegWrite(mem_wb_1_regwrite_2), .CLK(not_1_out), .Reset(RST));
  ID_EX id_ex_1 (
    .RegDst(multiplexer_4_out[2:1]), .Branch(multiplexer_4_out[3]), .Jump(multiplexer_4_out[5:4]),
    .ALUop(multiplexer_4_out[7:6]), .MemToReg(multiplexer_4_out[9:8]), .MemRead(multiplexer_4_out[10]),
    .MemWrite(multiplexer_4_out[11]), .ALUSrc(multiplexer_4_out[12]), .RegWrite(multiplexer_4_out[13]),
    .RD1(regfile_1_regdata1), .RD2(regfile_1_regdata2), .Immediate(bit_extender_1_out),
    .Func(if_id_1_out_6[3:0]), .RegDst_2(id_ex_1_regdst_2), .out_26(id_ex_1_out_26), .out_27(id_ex_1_out_27),
    .ALUop_2(id_ex_1_aluop_2), .MemToReg_2(id_ex_1_memtoreg_2), .MemRead_2(id_ex_1_memread_2),
    .MemWrite_2(id_ex_1_memwrite_2), .ALUSrc_2(id_ex_1_alusrc_2), .RegWrite_2(id_ex_1_regwrite_2),
    .RD1_2(id_ex_1_rd1_2), .RD2_2(id_ex_1_rd2_2), .Immediate_2(id_ex_1_immediate_2), .Func_2(id_ex_1_func_2),
    .CLK(CLK), .RST(or_3_out), .Address(if_id_1_out_6[15:0]), .Address_2(id_ex_1_address_2),
    .rt(if_id_1_out_6[11:8]), .rt_2(id_ex_1_rt_2), .rd(if_id_1_out_6[7:4]), .rd_2(id_ex_1_rd_2),
    .PC_1(if_id_1_out_7), .PC_1_2(id_ex_1_pc_1_2), .rs(if_id_1_out_6[15:12]), .rs_2(id_ex_1_rs_2),
    .Flush(multiplexer_4_out[0]), .Flush_2(id_ex_1_flush_2));
  or or_3 (or_3_out, Flush, RST);
  Multiplexer #(.select(2), .width(16), .enable("false")) multiplexer_5 (
    .in0(id_ex_1_rd2_2), .in1(multiplexer_9_out), .in2(ex_mem_1_result_2), .out(multiplexer_5_out),
    .sel(forwardingunit_1_forwardb));  // open: in3
  alucontrol alucontrol_1 (.ALUOp(id_ex_1_aluop_2), .Func(id_ex_1_func_2), .out_3(alucontrol_1_out_3));
  Adder #(.width(16)) adder_2 (.a(id_ex_1_pc_1_2), .b(id_ex_1_immediate_2), .out(adder_2_out));  // open: cin, cout
  Multiplexer #(.select(2), .width(16), .enable("false")) multiplexer_6 (
    .in0(id_ex_1_rd1_2), .in1(multiplexer_9_out), .in2(ex_mem_1_result_2), .out(multiplexer_6_out),
    .sel(forwardingunit_1_forwarda));  // open: in3
  Multiplexer #(.width(16), .enable("false")) multiplexer_7 (
    .in0(multiplexer_5_out), .in1(id_ex_1_immediate_2), .out(multiplexer_7_out), .sel(id_ex_1_alusrc_2));
  ForwardingUnit forwardingunit_1 (
    .ID_EX_RegisterRS(id_ex_1_rs_2), .ID_EX_RegisterRt(id_ex_1_rt_2), .MEM_WB_RegWrite(mem_wb_1_regwrite_2),
    .EX_MEM_RegWrite(ex_mem_1_regwrite_2), .EX_MEM_RegisterRd(ex_mem_1_rd_2),
    .MEM_WB_RegisterRd(mem_wb_1_rd_2), .ForwardA(forwardingunit_1_forwarda),
    .ForwardB(forwardingunit_1_forwardb));
  ALU16 alu16_1 (
    .aluop(alucontrol_1_out_3), .in_2(multiplexer_6_out), .in_3(multiplexer_7_out), .zero(alu16_1_zero),
    .result(alu16_1_result));  // open: oflow
  EX_MEM ex_mem_1 (
    .BranchAddress(adder_2_out), .Address(id_ex_1_address_2), .Branch(id_ex_1_out_26), .Jump(id_ex_1_out_27),
    .MemToReg(id_ex_1_memtoreg_2), .MemRead(id_ex_1_memread_2), .MemWrite(id_ex_1_memwrite_2),
    .RegWrite(id_ex_1_regwrite_2), .RD2(multiplexer_5_out), .rd(multiplexer_8_out),
    .BranchAdress(ex_mem_1_branchadress), .Address_2(ex_mem_1_address_2), .out_23(ex_mem_1_out_23),
    .out_24(ex_mem_1_out_24), .MemToReg_2(ex_mem_1_memtoreg_2), .MemRead_2(ex_mem_1_memread_2),
    .MemWrite_2(ex_mem_1_memwrite_2), .RegWrite_2(ex_mem_1_regwrite_2), .RD2_2(ex_mem_1_rd2_2),
    .rd_2(ex_mem_1_rd_2), .CLK(CLK), .RST(or_4_out), .zero(alu16_1_zero), .zero_2(ex_mem_1_zero_2),
    .result(alu16_1_result), .result_2(ex_mem_1_result_2), .PC_1(id_ex_1_pc_1_2), .PC_1_2(ex_mem_1_pc_1_2),
    .r1(id_ex_1_rd1_2), .r1_2(ex_mem_1_r1_2), .Flush(id_ex_1_flush_2), .Flush_2(Flush_2));
  Multiplexer #(.select(2), .width(4), .enable("false")) multiplexer_8 (
    .in0(id_ex_1_rt_2), .in1(id_ex_1_rd_2), .in2(4'b1111), .out(multiplexer_8_out), .sel(id_ex_1_regdst_2));  // open: in3
  buf or_4 (or_4_out, RST);  // OR_Gate
  not not_2 (not_2_out, CLK);
  MEM_WB mem_wb_1 (
    .MemToReg(ex_mem_1_memtoreg_2), .RegWrite(ex_mem_1_regwrite_2), .rd(ex_mem_1_rd_2),
    .MemToReg_2(mem_wb_1_memtoreg_2), .RegWrite_2(mem_wb_1_regwrite_2), .rd_2(mem_wb_1_rd_2), .CLK(CLK),
    .RST(RST), .data(ram_1_data), .data_2(mem_wb_1_data_2), .result(ex_mem_1_result_2),
    .result_2(mem_wb_1_result_2), .pc_1(ex_mem_1_pc_1_2), .pc_1_2(mem_wb_1_pc_1_2));
  RAM #(.addrWidth(16), .dataWidth(16), .bus("separate")) ram_1 (
    .addr(ex_mem_1_result_2), .din(ex_mem_1_rd2_2), .data(ram_1_data), .str(ex_mem_1_memwrite_2),
    .clk(not_2_out), .ld(ex_mem_1_memread_2), .clr(RST));  // open: sel
  Multiplexer #(.select(2), .width(16), .enable("false")) multiplexer_9 (
    .in0(mem_wb_1_result_2), .in1(mem_wb_1_data_2), .in2(mem_wb_1_pc_1_2), .out(multiplexer_9_out),
    .sel(mem_wb_1_memtoreg_2));  // open: in3

  // Notes on the sheet:
  //   contents of rom_1 (hex, n*v repeats v):
  //   30eff 30402 60005 5d200 1001a 3eefd 5eb00 5e401 5ef02 30102 4117 21003 30201 3ee03 7f000 344ff 60005
  //   20b2 344ff 60005 2b22 4eb00 4e401 4ef02 3ee03 7f000
endmodule

module adder1bit (
  input  C_in,
  input  A,
  input  B,
  output S,
  output C_out
);

  wire and_1_out, and_2_out, xor_1_out;

  xor xor_1 (xor_1_out, A, B);
  and and_1 (and_1_out, A, B);
  xor xor_2 (S, xor_1_out, C_in);
  and and_2 (and_2_out, xor_1_out, C_in);
  or or_1 (C_out, and_2_out, and_1_out);
endmodule

module alu1 (
  input  a_invert,
  input  b_invert,
  input  [1:0] op,
  input  C_in,
  input  A,
  input  B,
  input  less,
  output out,
  output C_out
);

  wire add_out, adder1bit_1_s, and_1_out, and_2_out, and_3_out, and_4_out, and_5_out, and_6_out, less_out,
       not_1_out, not_2_out, not_3_out, not_4_out, not_5_out, not_6_out, or_1_out, or_2_out, or_3_out,
       or_4_out;

  not not_1 (not_1_out, a_invert);
  not not_2 (not_2_out, A);
  not not_3 (not_3_out, B);
  not not_4 (not_4_out, b_invert);
  and and_1 (and_1_out, A, not_1_out);
  and and_2 (and_2_out, a_invert, not_2_out);
  and and_3 (and_3_out, not_4_out, B);
  or or_1 (or_1_out, and_3_out, and_4_out);
  and and_4 (and_4_out, b_invert, not_3_out);
  and and_5 (and_5_out, or_2_out, or_1_out);
  or or_2 (or_2_out, and_1_out, and_2_out);
  or or_3 (or_3_out, or_2_out, or_1_out);
  adder1bit adder1bit_1 (.A(or_2_out), .B(or_1_out), .S(adder1bit_1_s), .C_in(C_in), .C_out(C_out));
  not not_5 (not_5_out, op[0]);
  not not_6 (not_6_out, op[1]);
  and and_6 (and_6_out, not_5_out, not_6_out, and_5_out);
  and or_4 (or_4_out, op[0], or_3_out, not_6_out);
  and add (add_out, not_5_out, adder1bit_1_s, op[1]);
  and u_less (less_out, op[0], less, op[1]);
  or or_5 (out, and_6_out, or_4_out, add_out, less_out);
endmodule

module aluMSB (
  input  [1:0] op,
  input  a_invert,
  input  b_invert,
  input  C_in,
  input  A,
  input  B,
  input  less,
  output out,
  output set,
  output oflow
);

  wire add_out, adder1bit_1_c_out, and_1_out, and_2_out, and_3_out, and_4_out, and_5_out, and_6_out,
       less_out, not_1_out, not_2_out, not_3_out, not_4_out, not_5_out, not_6_out, or_1_out, or_2_out,
       or_3_out, or_4_out;

  not not_1 (not_1_out, a_invert);
  not not_2 (not_2_out, b_invert);
  not not_3 (not_3_out, A);
  not not_4 (not_4_out, B);
  and and_1 (and_1_out, A, not_1_out);
  or or_1 (or_1_out, and_1_out, and_2_out);
  and and_2 (and_2_out, a_invert, not_3_out);
  and and_3 (and_3_out, not_2_out, B);
  or or_2 (or_2_out, and_3_out, and_4_out);
  and and_4 (and_4_out, b_invert, not_4_out);
  aluOflow aluoflow_1 (.b_inv(b_invert), .a(or_1_out), .b(or_2_out), .c_in(adder1bit_1_c_out), .s(set), .out_6(oflow));
  and and_5 (and_5_out, or_1_out, or_2_out);
  or or_3 (or_3_out, or_1_out, or_2_out);
  adder1bit adder1bit_1 (.A(or_1_out), .B(or_2_out), .S(set), .C_in(C_in), .C_out(adder1bit_1_c_out));
  not not_5 (not_5_out, op[1]);
  not not_6 (not_6_out, op[0]);
  and and_6 (and_6_out, not_6_out, not_5_out, and_5_out);
  and or_4 (or_4_out, op[0], or_3_out, not_5_out);
  and add (add_out, not_6_out, set, op[1]);
  and u_less (less_out, op[0], less, op[1]);
  or or_5 (out, and_6_out, or_4_out, add_out, less_out);
endmodule

module aluOflow (
  input  b_inv,
  input  a,
  input  b,
  input  c_in,
  input  s,
  output out_6
);

  wire xnor_1_out, xor_1_out;

  xnor xnor_1 (xnor_1_out, a, b);
  and and_1 (out_6, xnor_1_out, xor_1_out);
  xor xor_1 (xor_1_out, c_in, s);
endmodule

module ALU16 (
  input  [3:0] aluop,
  input  [15:0] in_2,
  input  [15:0] in_3,
  output zero,
  output [15:0] result,
  output oflow
);

  wire alu1_1_c_out, alu1_2_c_out, alu1_3_c_out, alu1_4_c_out, alu1_5_c_out, alu1_6_c_out, alu1_7_c_out,
       alu1_8_c_out, alu1_9_c_out, alu1_10_c_out, alu1_11_c_out, alu1_12_c_out, alu1_13_c_out, alu1_14_c_out,
       alu1_15_c_out, alumsb_1_set, or_1_out;

  alu1 alu1_1 (
    .A(aluop[3]), .B(in_3[0]), .out(result[0]), .b_invert(aluop[2]), .C_in(aluop[2]), .op(aluop[1:0]),
    .C_out(alu1_1_c_out), .a_invert(in_2[0]), .less(alumsb_1_set));
  alu1 alu1_2 (
    .A(aluop[3]), .B(in_3[1]), .out(result[1]), .b_invert(aluop[2]), .C_in(alu1_1_c_out), .op(aluop[1:0]),
    .C_out(alu1_2_c_out), .a_invert(in_2[1]), .less(1'b0));
  alu1 alu1_3 (
    .A(aluop[3]), .B(in_3[2]), .out(result[2]), .b_invert(aluop[2]), .C_in(alu1_2_c_out), .op(aluop[1:0]),
    .C_out(alu1_3_c_out), .a_invert(in_2[2]), .less(1'b0));
  alu1 alu1_4 (
    .A(aluop[3]), .B(in_3[3]), .out(result[3]), .b_invert(aluop[2]), .C_in(alu1_3_c_out), .op(aluop[1:0]),
    .C_out(alu1_4_c_out), .a_invert(in_2[3]), .less(1'b0));
  alu1 alu1_5 (
    .A(aluop[3]), .B(in_3[4]), .out(result[4]), .b_invert(aluop[2]), .C_in(alu1_4_c_out), .op(aluop[1:0]),
    .C_out(alu1_5_c_out), .a_invert(in_2[4]), .less(1'b0));
  alu1 alu1_6 (
    .A(aluop[3]), .B(in_3[5]), .out(result[5]), .b_invert(aluop[2]), .C_in(alu1_5_c_out), .op(aluop[1:0]),
    .C_out(alu1_6_c_out), .a_invert(in_2[5]), .less(1'b0));
  alu1 alu1_7 (
    .A(aluop[3]), .B(in_3[6]), .out(result[6]), .b_invert(aluop[2]), .C_in(alu1_6_c_out), .op(aluop[1:0]),
    .C_out(alu1_7_c_out), .a_invert(in_2[6]), .less(1'b0));
  alu1 alu1_8 (
    .A(aluop[3]), .B(in_3[7]), .out(result[7]), .b_invert(aluop[2]), .C_in(alu1_7_c_out), .op(aluop[1:0]),
    .C_out(alu1_8_c_out), .a_invert(in_2[7]), .less(1'b0));
  alu1 alu1_9 (
    .A(aluop[3]), .B(in_3[8]), .out(result[8]), .b_invert(aluop[2]), .C_in(alu1_8_c_out), .op(aluop[1:0]),
    .C_out(alu1_9_c_out), .a_invert(in_2[8]), .less(1'b0));
  alu1 alu1_10 (
    .A(aluop[3]), .B(in_3[9]), .out(result[9]), .b_invert(aluop[2]), .C_in(alu1_9_c_out), .op(aluop[1:0]),
    .C_out(alu1_10_c_out), .a_invert(in_2[9]), .less(1'b0));
  alu1 alu1_11 (
    .A(aluop[3]), .B(in_3[10]), .out(result[10]), .b_invert(aluop[2]), .C_in(alu1_10_c_out), .op(aluop[1:0]),
    .C_out(alu1_11_c_out), .a_invert(in_2[10]), .less(1'b0));
  alu1 alu1_12 (
    .A(aluop[3]), .B(in_3[11]), .out(result[11]), .b_invert(aluop[2]), .C_in(alu1_11_c_out), .op(aluop[1:0]),
    .C_out(alu1_12_c_out), .a_invert(in_2[11]), .less(1'b0));
  alu1 alu1_13 (
    .A(aluop[3]), .B(in_3[12]), .out(result[12]), .b_invert(aluop[2]), .C_in(alu1_12_c_out), .op(aluop[1:0]),
    .C_out(alu1_13_c_out), .a_invert(in_2[12]), .less(1'b0));
  alu1 alu1_14 (
    .A(aluop[3]), .B(in_3[13]), .out(result[13]), .b_invert(aluop[2]), .C_in(alu1_13_c_out), .op(aluop[1:0]),
    .C_out(alu1_14_c_out), .a_invert(in_2[13]), .less(1'b0));
  alu1 alu1_15 (
    .A(aluop[3]), .B(in_3[14]), .out(result[14]), .b_invert(aluop[2]), .C_in(alu1_14_c_out), .op(aluop[1:0]),
    .C_out(alu1_15_c_out), .a_invert(in_2[14]), .less(1'b0));
  aluMSB alumsb_1 (
    .A(in_2[15]), .B(in_3[15]), .less(1'b0), .out(result[15]), .set(alumsb_1_set), .oflow(oflow),
    .a_invert(aluop[3]), .b_invert(aluop[2]), .C_in(alu1_15_c_out), .op(aluop[1:0]));
  or or_1 (or_1_out, result[8], result[9], result[10], result[11], result[12], result[13], result[14], result[15], result[0], result[1], result[2], result[3], result[4], result[5], result[6], result[7]);
  not not_1 (zero, or_1_out);
endmodule

module _3bitEquality (
  input  [2:0] in_1,
  input  [2:0] in_2,
  output out_3
);

  wire [2:0] xnor_1_out;

  assign xnor_1_out = ~(in_1 ^ in_2);  // XNOR_Gate xnor_1, 3 bits wide
  and and_1 (out_3, xnor_1_out[0], xnor_1_out[1], xnor_1_out[2]);
endmodule

module control (
  input  [2:0] OP,
  output IF_Flush,
  output [1:0] RegDst,
  output Branch,
  output [1:0] Jump,
  output [1:0] ALUOp,
  output [1:0] MemtoReg,
  output MemRead,
  output MemWrite,
  output ALUSrc,
  output RegWrite
);

  wire n3bitequality_5_out_3, n3bitequality_7_out_3, or_2_out;
  wire [1:0] and_1_out, and_2_out, and_3_out, bit_extender_1_out, bit_extender_2_out, bit_extender_3_out;

  _3bitEquality u_3bitequality_1 (.in_1(3'b111), .in_2(OP), .out_3(Jump[1]));
  _3bitEquality u_3bitequality_2 (.in_1(3'b110), .in_2(OP), .out_3(MemtoReg[1]));
  _3bitEquality u_3bitequality_3 (.in_1(3'b101), .in_2(OP), .out_3(MemWrite));
  _3bitEquality u_3bitequality_4 (.in_1(3'b100), .in_2(OP), .out_3(MemRead));
  _3bitEquality u_3bitequality_5 (.in_1(3'b011), .in_2(OP), .out_3(n3bitequality_5_out_3));
  _3bitEquality u_3bitequality_6 (.in_1(3'b010), .in_2(OP), .out_3(Branch));
  _3bitEquality u_3bitequality_7 (.in_1(3'b001), .in_2(OP), .out_3(n3bitequality_7_out_3));
  _3bitEquality u_3bitequality_8 (.in_1(3'b000), .in_2(OP), .out_3(RegDst[0]));
  or or_1 (IF_Flush, Jump[1], n3bitequality_7_out_3, MemtoReg[1]);
  or or_2 (or_2_out, MemRead, MemWrite, n3bitequality_5_out_3);
  assign bit_extender_1_out = {{1{Branch}}, Branch};  // Bit_Extender bit_extender_1
  assign bit_extender_2_out = {{1{or_2_out}}, or_2_out};  // Bit_Extender bit_extender_2
  assign bit_extender_3_out = {{1{RegDst[0]}}, RegDst[0]};  // Bit_Extender bit_extender_3
  or or_3 (Jump[0], n3bitequality_7_out_3, MemtoReg[1]);
  assign and_1_out = bit_extender_1_out & 2'b01;  // AND_Gate and_1, 2 bits wide
  assign ALUOp = and_1_out | and_2_out | and_3_out;  // OR_Gate or_4, 2 bits wide
  assign and_2_out = bit_extender_2_out & 2'b00;  // AND_Gate and_2, 2 bits wide
  assign and_3_out = bit_extender_3_out & 2'b10;  // AND_Gate and_3, 2 bits wide
  or or_5 (ALUSrc, MemRead, MemWrite, n3bitequality_5_out_3);
  or or_6 (RegWrite, MemRead, n3bitequality_5_out_3, RegDst[0], MemtoReg[1]);

  assign MemtoReg[0] = MemRead;
  assign RegDst[1] = MemtoReg[1];

  // Notes on the sheet:
  //   jr
  //   jal
  //   sw
  //   lw
  //   addi
  //   beq
  //   j
  //   R Type
endmodule

module alucontrol (
  input  [1:0] ALUOp,
  input  [3:0] Func,
  output [3:0] out_3
);

  wire n2biteq_1_out_3, n2biteq_2_out_3, n2biteq_3_out_3;

  _2bitEq u_2biteq_1 (.in_1(ALUOp), .in_2(2'b00), .out_3(n2biteq_1_out_3));
  _2bitEq u_2biteq_2 (.in_1(ALUOp), .in_2(2'b01), .out_3(n2biteq_2_out_3));
  _2bitEq u_2biteq_3 (.in_1(ALUOp), .in_2(2'b10), .out_3(n2biteq_3_out_3));
  assign out_3 = n2biteq_1_out_3 ? 4'b0010 : 4'bz;  // Controlled_Buffer controlled_buffer_1
  assign out_3 = n2biteq_2_out_3 ? 4'b0110 : 4'bz;  // Controlled_Buffer controlled_buffer_2
  assign out_3 = n2biteq_3_out_3 ? Func : 4'bz;  // Controlled_Buffer controlled_buffer_3
endmodule

module _2bitEq (
  input  [1:0] in_1,
  input  [1:0] in_2,
  output out_3
);

  wire [1:0] xnor_1_out;

  assign xnor_1_out = ~(in_1 ^ in_2);  // XNOR_Gate xnor_1, 2 bits wide
  and and_1 (out_3, xnor_1_out[0], xnor_1_out[1]);
endmodule

module RegFile (
  input  RegWrite,
  input  [3:0] RegRead1,
  input  [3:0] RegRead2,
  input  [3:0] RegWrite_2,
  input  [15:0] DIn,
  input  CLK,
  input  Reset,
  output [15:0] RegData1,
  output [15:0] RegData2
);

  wire decoder_1_out0, decoder_1_out1, decoder_1_out2, decoder_1_out3, decoder_1_out4, decoder_1_out5,
       decoder_1_out6, decoder_1_out7, decoder_1_out8, decoder_1_out9, decoder_1_out10, decoder_1_out11,
       decoder_1_out12, decoder_1_out13, decoder_1_out14, decoder_1_out15;
  wire [15:0] register_1_q, register_2_q, register_3_q, register_4_q, register_5_q, register_6_q,
       register_7_q, register_8_q, register_9_q, register_10_q, register_11_q, register_12_q, register_13_q,
       register_14_q, register_15_q, register_16_q;

  Decoder #(.select(4), .disabled(0)) decoder_1 (
    .out0(decoder_1_out0), .out1(decoder_1_out1), .out2(decoder_1_out2), .out3(decoder_1_out3),
    .out4(decoder_1_out4), .out5(decoder_1_out5), .out6(decoder_1_out6), .out7(decoder_1_out7),
    .out8(decoder_1_out8), .out9(decoder_1_out9), .out10(decoder_1_out10), .out11(decoder_1_out11),
    .out12(decoder_1_out12), .out13(decoder_1_out13), .out14(decoder_1_out14), .out15(decoder_1_out15),
    .sel(RegWrite_2), .en(RegWrite));
  Register #(.width(16)) register_1 (.D(DIn), .en(decoder_1_out0), .Q(register_1_q), .clk(CLK), .clr(Reset));
  Register #(.width(16)) register_2 (.D(DIn), .en(decoder_1_out1), .Q(register_2_q), .clk(CLK), .clr(Reset));
  Register #(.width(16)) register_3 (.D(DIn), .en(decoder_1_out2), .Q(register_3_q), .clk(CLK), .clr(Reset));
  Register #(.width(16)) register_4 (.D(DIn), .en(decoder_1_out3), .Q(register_4_q), .clk(CLK), .clr(Reset));
  Register #(.width(16)) register_5 (.D(DIn), .en(decoder_1_out4), .Q(register_5_q), .clk(CLK), .clr(Reset));
  Register #(.width(16)) register_6 (.D(DIn), .en(decoder_1_out5), .Q(register_6_q), .clk(CLK), .clr(Reset));
  Register #(.width(16)) register_7 (.D(DIn), .en(decoder_1_out6), .Q(register_7_q), .clk(CLK), .clr(Reset));
  Register #(.width(16)) register_8 (.D(DIn), .en(decoder_1_out7), .Q(register_8_q), .clk(CLK), .clr(Reset));
  Register #(.width(16)) register_9 (.D(DIn), .en(decoder_1_out8), .Q(register_9_q), .clk(CLK), .clr(Reset));
  Register #(.width(16)) register_10 (.D(DIn), .en(decoder_1_out9), .Q(register_10_q), .clk(CLK), .clr(Reset));
  Register #(.width(16)) register_11 (.D(DIn), .en(decoder_1_out10), .Q(register_11_q), .clk(CLK), .clr(Reset));
  Register #(.width(16)) register_12 (.D(DIn), .en(decoder_1_out11), .Q(register_12_q), .clk(CLK), .clr(Reset));
  Register #(.width(16)) register_13 (.D(DIn), .en(decoder_1_out12), .Q(register_13_q), .clk(CLK), .clr(Reset));
  Register #(.width(16)) register_14 (.D(DIn), .en(decoder_1_out13), .Q(register_14_q), .clk(CLK), .clr(Reset));
  Register #(.width(16)) register_15 (.D(DIn), .en(decoder_1_out14), .Q(register_15_q), .clk(CLK), .clr(Reset));
  Register #(.width(16)) register_16 (.D(DIn), .en(decoder_1_out15), .Q(register_16_q), .clk(CLK), .clr(Reset));
  Multiplexer #(.select(4), .width(16), .enable("false")) multiplexer_1 (
    .in0(register_1_q), .in1(register_2_q), .in2(register_3_q), .in3(register_4_q), .in4(register_5_q),
    .in5(register_6_q), .in6(register_7_q), .in7(register_8_q), .in8(register_9_q), .in9(register_10_q),
    .in10(register_11_q), .in11(register_12_q), .in12(register_13_q), .in13(register_14_q),
    .in14(register_15_q), .in15(register_16_q), .out(RegData1), .sel(RegRead1));
  Multiplexer #(.select(4), .width(16), .enable("false")) multiplexer_2 (
    .in0(register_1_q), .in1(register_2_q), .in2(register_3_q), .in3(register_4_q), .in4(register_5_q),
    .in5(register_6_q), .in6(register_7_q), .in7(register_8_q), .in8(register_9_q), .in9(register_10_q),
    .in10(register_11_q), .in11(register_12_q), .in12(register_13_q), .in13(register_14_q),
    .in14(register_15_q), .in15(register_16_q), .out(RegData2), .sel(RegRead2));

  // Notes on the sheet:
  //   0: $0
endmodule

module IF_ID (
  input  Write,
  input  [18:0] in_2,
  input  [15:0] in_3,
  input  CLK,
  input  RST,
  output [18:0] out_6,
  output [15:0] out_7
);

  Register #(.width(19)) register_1 (.D(in_2), .en(Write), .Q(out_6), .clk(CLK), .clr(RST));
  Register #(.width(16)) register_2 (.D(in_3), .en(Write), .Q(out_7), .clk(CLK), .clr(RST));
endmodule

module ID_EX (
  input  [15:0] PC_1,
  input  Flush,
  input  [15:0] Address,
  input  [1:0] RegDst,
  input  Branch,
  input  [1:0] Jump,
  input  [1:0] ALUop,
  input  [1:0] MemToReg,
  input  MemRead,
  input  MemWrite,
  input  ALUSrc,
  input  RegWrite,
  input  [15:0] RD1,
  input  [15:0] RD2,
  input  [3:0] rt,
  input  [3:0] rd,
  input  [15:0] Immediate,
  input  [3:0] Func,
  input  [3:0] rs,
  input  RST,
  input  CLK,
  output [15:0] PC_1_2,
  output Flush_2,
  output [15:0] Address_2,
  output [1:0] RegDst_2,
  output out_26,
  output [1:0] out_27,
  output [1:0] ALUop_2,
  output [1:0] MemToReg_2,
  output MemRead_2,
  output MemWrite_2,
  output ALUSrc_2,
  output RegWrite_2,
  output [15:0] RD1_2,
  output [15:0] RD2_2,
  output [3:0] rt_2,
  output [3:0] rd_2,
  output [15:0] Immediate_2,
  output [3:0] Func_2,
  output [3:0] rs_2
);

  Register #(.width(16)) register_1 (.D(PC_1), .en(1'b1), .Q(PC_1_2), .clk(CLK), .clr(RST));
  Register #(.width(1)) register_2 (.D(Flush), .en(1'b1), .Q(Flush_2), .clk(CLK), .clr(RST));
  Register #(.width(16)) register_3 (.D(Address), .en(1'b1), .Q(Address_2), .clk(CLK), .clr(RST));
  Register #(.width(2)) register_4 (.D(RegDst), .en(1'b1), .Q(RegDst_2), .clk(CLK), .clr(RST));
  Register #(.width(1)) register_5 (.D(Branch), .en(1'b1), .Q(out_26), .clk(CLK), .clr(RST));
  Register #(.width(2)) register_6 (.D(Jump), .en(1'b1), .Q(out_27), .clk(CLK), .clr(RST));
  Register #(.width(2)) register_7 (.D(ALUop), .en(1'b1), .Q(ALUop_2), .clk(CLK), .clr(RST));
  Register #(.width(2)) register_8 (.D(MemToReg), .en(1'b1), .Q(MemToReg_2), .clk(CLK), .clr(RST));
  Register #(.width(1)) register_9 (.D(MemRead), .en(1'b1), .Q(MemRead_2), .clk(CLK), .clr(RST));
  Register #(.width(1)) register_10 (.D(MemWrite), .en(1'b1), .Q(MemWrite_2), .clk(CLK), .clr(RST));
  Register #(.width(1)) register_11 (.D(ALUSrc), .en(1'b1), .Q(ALUSrc_2), .clk(CLK), .clr(RST));
  Register #(.width(1)) register_12 (.D(RegWrite), .en(1'b1), .Q(RegWrite_2), .clk(CLK), .clr(RST));
  Register #(.width(16)) register_13 (.D(RD1), .en(1'b1), .Q(RD1_2), .clk(CLK), .clr(RST));
  Register #(.width(16)) register_14 (.D(RD2), .en(1'b1), .Q(RD2_2), .clk(CLK), .clr(RST));
  Register #(.width(4)) register_15 (.D(rt), .en(1'b1), .Q(rt_2), .clk(CLK), .clr(RST));
  Register #(.width(4)) register_16 (.D(rd), .en(1'b1), .Q(rd_2), .clk(CLK), .clr(RST));
  Register #(.width(16)) register_17 (.D(Immediate), .en(1'b1), .Q(Immediate_2), .clk(CLK), .clr(RST));
  Register #(.width(4)) register_18 (.D(Func), .en(1'b1), .Q(Func_2), .clk(CLK), .clr(RST));
  Register #(.width(4)) register_19 (.D(rs), .en(1'b1), .Q(rs_2), .clk(CLK), .clr(RST));
endmodule

module EX_MEM (
  input  [15:0] r1,
  input  [15:0] PC_1,
  input  [15:0] BranchAddress,
  input  [15:0] Address,
  input  Flush,
  input  Branch,
  input  [1:0] Jump,
  input  [1:0] MemToReg,
  input  MemRead,
  input  MemWrite,
  input  RegWrite,
  input  zero,
  input  [15:0] result,
  input  [15:0] RD2,
  input  [3:0] rd,
  input  CLK,
  input  RST,
  output [15:0] r1_2,
  output [15:0] PC_1_2,
  output [15:0] BranchAdress,
  output [15:0] Address_2,
  output Flush_2,
  output out_23,
  output [1:0] out_24,
  output [1:0] MemToReg_2,
  output MemRead_2,
  output MemWrite_2,
  output RegWrite_2,
  output zero_2,
  output [15:0] result_2,
  output [15:0] RD2_2,
  output [3:0] rd_2
);

  Register #(.width(16)) register_1 (.D(r1), .en(1'b1), .Q(r1_2), .clk(CLK), .clr(RST));
  Register #(.width(16)) register_2 (.D(PC_1), .en(1'b1), .Q(PC_1_2), .clk(CLK), .clr(RST));
  Register #(.width(16)) register_3 (.D(BranchAddress), .en(1'b1), .Q(BranchAdress), .clk(CLK), .clr(RST));
  Register #(.width(16)) register_4 (.D(Address), .en(1'b1), .Q(Address_2), .clk(CLK), .clr(RST));
  Register #(.width(1)) register_5 (.D(Flush), .en(1'b1), .Q(Flush_2), .clk(CLK), .clr(RST));
  Register #(.width(1)) register_6 (.D(Branch), .en(1'b1), .Q(out_23), .clk(CLK), .clr(RST));
  Register #(.width(2)) register_7 (.D(Jump), .en(1'b1), .Q(out_24), .clk(CLK), .clr(RST));
  Register #(.width(2)) register_8 (.D(MemToReg), .en(1'b1), .Q(MemToReg_2), .clk(CLK), .clr(RST));
  Register #(.width(1)) register_9 (.D(MemRead), .en(1'b1), .Q(MemRead_2), .clk(CLK), .clr(RST));
  Register #(.width(1)) register_10 (.D(MemWrite), .en(1'b1), .Q(MemWrite_2), .clk(CLK), .clr(RST));
  Register #(.width(1)) register_11 (.D(RegWrite), .en(1'b1), .Q(RegWrite_2), .clk(CLK), .clr(RST));
  Register #(.width(1)) register_12 (.D(zero), .en(1'b1), .Q(zero_2), .clk(CLK), .clr(RST));
  Register #(.width(16)) register_13 (.D(result), .en(1'b1), .Q(result_2), .clk(CLK), .clr(RST));
  Register #(.width(16)) register_14 (.D(RD2), .en(1'b1), .Q(RD2_2), .clk(CLK), .clr(RST));
  Register #(.width(4)) register_15 (.D(rd), .en(1'b1), .Q(rd_2), .clk(CLK), .clr(RST));
endmodule

module MEM_WB (
  input  [15:0] pc_1,
  input  [15:0] result,
  input  [15:0] data,
  input  [1:0] MemToReg,
  input  RegWrite,
  input  [3:0] rd,
  input  CLK,
  input  RST,
  output [15:0] pc_1_2,
  output [15:0] result_2,
  output [15:0] data_2,
  output [1:0] MemToReg_2,
  output RegWrite_2,
  output [3:0] rd_2
);

  Register #(.width(16)) register_1 (.D(pc_1), .en(1'b1), .Q(pc_1_2), .clk(CLK), .clr(RST));
  Register #(.width(16)) register_2 (.D(result), .en(1'b1), .Q(result_2), .clk(CLK), .clr(RST));
  Register #(.width(16)) register_3 (.D(data), .en(1'b1), .Q(data_2), .clk(CLK), .clr(RST));
  Register #(.width(2)) register_4 (.D(MemToReg), .en(1'b1), .Q(MemToReg_2), .clk(CLK), .clr(RST));
  Register #(.width(1)) register_5 (.D(RegWrite), .en(1'b1), .Q(RegWrite_2), .clk(CLK), .clr(RST));
  Register #(.width(4)) register_6 (.D(rd), .en(1'b1), .Q(rd_2), .clk(CLK), .clr(RST));
endmodule

module _4bitEq (
  input  [3:0] in_1,
  input  [3:0] in_2,
  output out_3
);

  wire [3:0] xnor_1_out;

  assign xnor_1_out = ~(in_1 ^ in_2);  // XNOR_Gate xnor_1, 4 bits wide
  and and_1 (out_3, xnor_1_out[0], xnor_1_out[1], xnor_1_out[2], xnor_1_out[3]);
endmodule

module Hazard_Detection (
  input  ID_EX_MemRead,
  input  [3:0] IF_ID_RegisterRs,
  input  [3:0] ID_EX_RegisterRt,
  input  [3:0] IF_ID_RegisterRt,
  output PCIFIDWrite,
  output MuxSel
);

  wire n4biteq_1_out_3, n4biteq_2_out_3, or_1_out;

  not not_1 (PCIFIDWrite, MuxSel);
  and and_1 (MuxSel, ID_EX_MemRead, or_1_out);
  or or_1 (or_1_out, n4biteq_1_out_3, n4biteq_2_out_3);
  _4bitEq u_4biteq_1 (.in_1(IF_ID_RegisterRs), .in_2(ID_EX_RegisterRt), .out_3(n4biteq_1_out_3));
  _4bitEq u_4biteq_2 (.in_1(IF_ID_RegisterRt), .in_2(ID_EX_RegisterRt), .out_3(n4biteq_2_out_3));
endmodule

module ForwardingUnit (
  input  MEM_WB_RegWrite,
  input  EX_MEM_RegWrite,
  input  [3:0] ID_EX_RegisterRS,
  input  [3:0] EX_MEM_RegisterRd,
  input  [3:0] ID_EX_RegisterRt,
  input  [3:0] MEM_WB_RegisterRd,
  output [1:0] ForwardB,
  output [1:0] ForwardA
);

  wire ERD_0_out_3, erd_irs_out_3, erd_irt_out_3, exhaz_2_out, exhaz_out, memhaz_2_out, memhaz_out,
       mrd_0_out_3, mrd_irs_out_3, mrd_irt_out_3, not_1_out, not_2_out, not_3_out, not_4_out, not_5_out,
       not_6_out, or_1_out, or_2_out;

  assign ForwardA = not_1_out ? 2'b00 : 2'bz;  // Controlled_Buffer controlled_buffer_1
  not not_1 (not_1_out, or_1_out);
  assign ForwardA = memhaz_out ? 2'b01 : 2'bz;  // Controlled_Buffer controlled_buffer_2
  assign ForwardA = exhaz_out ? 2'b10 : 2'bz;  // Controlled_Buffer controlled_buffer_3
  and exhaz (exhaz_out, not_2_out, EX_MEM_RegWrite, erd_irs_out_3);
  not not_2 (not_2_out, ERD_0_out_3);
  _4bitEq ERD_0 (.in_1(4'b0000), .in_2(EX_MEM_RegisterRd), .out_3(ERD_0_out_3));
  assign ForwardB = memhaz_2_out ? 2'b01 : 2'bz;  // Controlled_Buffer controlled_buffer_4
  or or_1 (or_1_out, exhaz_out, memhaz_out);
  and memhaz (memhaz_out, not_3_out, not_4_out, mrd_irs_out_3, MEM_WB_RegWrite);
  not not_3 (not_3_out, exhaz_out);
  not not_4 (not_4_out, mrd_0_out_3);
  _4bitEq mrd_0 (.in_1(4'b0000), .in_2(MEM_WB_RegisterRd), .out_3(mrd_0_out_3));
  _4bitEq erd_irs (.in_1(ID_EX_RegisterRS), .in_2(EX_MEM_RegisterRd), .out_3(erd_irs_out_3));
  assign ForwardB = not_5_out ? 2'b00 : 2'bz;  // Controlled_Buffer controlled_buffer_5
  not not_5 (not_5_out, or_2_out);
  or or_2 (or_2_out, exhaz_2_out, memhaz_2_out);
  assign ForwardB = exhaz_2_out ? 2'b10 : 2'bz;  // Controlled_Buffer controlled_buffer_6
  not not_6 (not_6_out, exhaz_2_out);
  and exhaz_2 (exhaz_2_out, not_2_out, EX_MEM_RegWrite, erd_irt_out_3);
  _4bitEq mrd_irs (.in_1(ID_EX_RegisterRS), .in_2(MEM_WB_RegisterRd), .out_3(mrd_irs_out_3));
  _4bitEq erd_irt (.in_1(EX_MEM_RegisterRd), .in_2(ID_EX_RegisterRt), .out_3(erd_irt_out_3));
  and memhaz_2 (memhaz_2_out, not_6_out, not_4_out, mrd_irt_out_3, MEM_WB_RegWrite);
  _4bitEq mrd_irt (.in_1(ID_EX_RegisterRt), .in_2(MEM_WB_RegisterRd), .out_3(mrd_irt_out_3));
endmodule

module _16eq (
  input  [15:0] in_1,
  input  [15:0] in_2,
  output out_3
);

  wire [15:0] xnor_1_out;

  assign xnor_1_out = ~(in_1 ^ in_2);  // XNOR_Gate xnor_1, 16 bits wide
  and and_1 (out_3, xnor_1_out[0], xnor_1_out[1], xnor_1_out[2], xnor_1_out[3], xnor_1_out[4], xnor_1_out[5], xnor_1_out[6], xnor_1_out[7], xnor_1_out[8], xnor_1_out[9], xnor_1_out[10], xnor_1_out[11], xnor_1_out[12], xnor_1_out[13], xnor_1_out[14], xnor_1_out[15]);
endmodule
